# Fritzing sketch PulseraCMD (saved by Fritzing 0.9.2b)
breadboards: 1

parts:
  VCC1 = Battery block 9V
  U1 = atmega328 [package=dip]
  IC1 = Voltage Regulator [package=to220-igo]
  C1 = Capacitor Polarized [package=nippon_f80]
  Y1 = CRYSTAL [package=hc49us]
  Parte1 = Bluetooth Mate Silver
  C2 = Capacitor [package=cap-pth-small2]
  C3 = Capacitor [package=cap-pth-small2]
  U2 = Vibration Motor- ROB-08449 [package=vibe-motor-10mm]
  J1 = Piezo Speaker

nets:
  N1: VCC1.-, U1.GND#7, U1.AREF, IC1.IN, C1.-, Parte1.GND, C2.1, C3.2, U2.+, J1.pin1
  N2: VCC1.+, IC1.GND
  N3: U1.D0_(RX), Parte1.TX_5V
  N4: U1.D1_(TX), Parte1.RX_5V
  VCC: U1.VCC, U1.D13, IC1.OUT, C1.+, Parte1.VCC
  N5: U1.XLAT1, Y1.1, C2.2
  N6: U1.XLAT2, Y1.2, C3.1
  N7: U1.D9_(PWM), U2.-
  N8: U1.D10_(PWM), J1.pin2
